# Fritzing sketch matrix_joystick (saved by Fritzing 0.9.10b)
breadboards: 1

parts:
  Part1 = Arduino Uno (Rev3)
  Part2 = Thumb Joystick
  8x8_LED_Modul_mit_MAX1 = 8x8 LED Modul mit MAX7219 [package=THT]

nets:
  N1: Part1.A0, Part2.HORZ
  N2: Part1.A1, Part2.VERT
  N3: Part1.D2, 8x8_LED_Modul_mit_MAX1.CS_Eingang
  N4: Part1.D3_PWM, 8x8_LED_Modul_mit_MAX1.CLK_Eingang
  N5: Part1.D4, 8x8_LED_Modul_mit_MAX1.DIN_Eingang
  5V: Part1.5V, Part2.VCC, 8x8_LED_Modul_mit_MAX1.VCC_Eingang
  GND: Part1.GND, Part2.GND, 8x8_LED_Modul_mit_MAX1.GND_Eingang

notes:
  reserved for
  I2C
  communication
