# Fritzing sketch nummerplaat (saved by Fritzing 0.9.10b)
breadboards: 1

parts:
  7_Segment1 = 7 Segment Display
  Part1 = Arduino Uno (Rev3)
  R1 = Resistor [tolerance=±5% resistance=220 package="0402 [SMD]"]
  S1 = SWITCH-MOMENTARY-2 [package=reed_switch_plastic]

nets:
  N1: 7_Segment1.Segment_G, Part1.D6_PWM
  N2: 7_Segment1.Segment_F, Part1.D7
  N3: 7_Segment1.common_anode, R1.Pin_1
  N4: 7_Segment1.Segment_E, Part1.D8
  N5: 7_Segment1.Segment_D, Part1.D9_PWM
  N6: 7_Segment1.Segment_C, Part1.D10_PWM/SS
  N7: 7_Segment1.Segment_B, Part1.D11_PWM/MOSI
  N8: 7_Segment1.Segment_A, Part1.D12/MISO
  N9: Part1.D13/SCK, S1.1
  N10: Part1.5V, S1.2
  N11: Part1.GND, R1.Pin_0
