# Fritzing sketch proefbuis_nummerplaat_morse (saved by Fritzing 0.9.10b)
breadboards: 1

parts:
  Part1 = Arduino Uno (Rev3)
  S1 = Pushbutton [package=THT]
  S2 = SWITCH-MOMENTARY-2 [package=reed_switch_plastic]
  7_Segment1 = 7 Segment Display
  7_Segment2 = 7 Segment Display
  R1 = Resistor [tolerance=±5% resistance=220 package="0805 [SMD]"]
  R2 = Resistor [tolerance=±5% resistance=220 package="0805 [SMD]"]
  R3 = Resistor [tolerance=±5% resistance=10k package="0805 [SMD]"]
  R4 = Resistor [tolerance=±5% power=0.25 resistance=10k package=THT]

nets:
  N1: Part1.D8, 7_Segment1.Segment_E
  N2: Part1.D9_PWM, 7_Segment1.Segment_D
  N3: Part1.D10_PWM/SS, 7_Segment1.Segment_C
  N4: Part1.D11_PWM/MOSI, 7_Segment1.Segment_B
  N5: Part1.D12/MISO, 7_Segment1.Segment_A#10
  N6: Part1.D2, 7_Segment2.Segment_DP
  N7: Part1.D3_PWM, S1.leg1, R4.Pin_0
  N8: Part1.D5_PWM, 7_Segment1.Segment_DP
  N9: Part1.D6_PWM, 7_Segment1.Segment_A#1
  N10: Part1.D7, 7_Segment1.Segment_F
  N11: Part1.5V, S1.leg0, S2.2
  N12: Part1.GND, 7_Segment2.common_cathode#3, R1.Pin_0, R2.Pin_0, R2.Pin_1, R3.Pin_1, R4.Pin_1
  N13: S2.1, R3.Pin_0
  N14: 7_Segment1.common_cathode#3, R1.Pin_1

notes:
  reserved for
  I2C
  communication
